# Fritzing sketch Car_Sparkfun01_servo (saved by Fritzing 0.9.2b)
breadboards: 1

parts:
  M1 = DC Motor  # not connected
  M2 = DC Motor  # not connected
  VCC1 = 4 x AAA Battery Mount
  U1 = EDISON  # not connected
  U2 = SWITCH_SPDT [package=kps-1290]
  J1 = Basic Servo  # not connected

nets:
  N1: VCC1.+, U2.P

notes:
  1.2x4 = 4.8V
  CONSOLE
  OTG
  ON/OFF
