# Fritzing sketch Edison_Arduino (saved by Fritzing 0.9.2b)
breadboards: 1

parts:
  M1 = DC Motor  # not connected
  M2 = DC Motor  # not connected
  U2 = SWITCH_SPDT [package=kps-1290]
  J1 = Basic Servo
  Part1 = Intel Edison Arduinobreakout
  VCC2 = Battery

nets:
  N1: U2.P, VCC2.+
  N2: J1.gnd, VCC2.-
  VCC: J1.vcc, Part1.5V
  N3: J1.pulse, Part1.D10_PWM/SS

notes:
  3.7x2 = 7.4V
  CONSOLE
  ON/OFF
  5V
  7.4V
