# Fritzing sketch Edison_Sparkfun_servo (saved by Fritzing 0.9.2b)
breadboards: 1

parts:
  M1 = DC Motor  # not connected
  M2 = DC Motor  # not connected
  U1 = EDISON  # not connected
  U2 = SWITCH_SPDT [package=kps-1290]
  J1 = Basic Servo  # not connected
  VCC1 = Battery

nets:
  N1: U2.P, VCC1.+

notes:
  3.7x2 = 7.4V
  CONSOLE
  OTG
  ON/OFF
